# Fritzing sketch Schematics (saved by Fritzing 1.0.5)

parts:
  Round_Display_for_XIAO1 = Seeed Studio Round Display for XIAO [chip_label=" Round Display for XIAO" package="DIP (Dual Inline) [THT]"]
  ESP32S1 = XIAO ESP32S3(SENCE) [chip_label=ESP32S3(sense)]
  M1 = DC Mini Metal Gear Motor  # not connected
  J1 = Power Jack [package=power_jack_pth_lock]
  D1 = Schottky Diode [part_number=1N5817 package="300 mil [THT]"]

nets:
  N1: Round_Display_for_XIAO1.D6, ESP32S1.D6
  3V3: Round_Display_for_XIAO1.3V3, ESP32S1.3V3
  GND: ESP32S1.GND, J1.GND
  N2: ESP32S1.5V, D1.cathode
  N3: J1.PWR, D1.anode

notes:
  schottky diode
  MX1508
  5v

custom parts:
  Seeed Studio Round Display for XIAO: Seeed Studio Round Display for XIAO is an expansion board compatible with all XIAO development boards. It features a fully covered touch screen on one side, designed as a 39mm disc. It contains onboard RTC, charge chip, TF card slot within its compact size, perfect for interactive displays in smart home, wearables and more.
  XIAO ESP32S3(SENCE): Seeed Studio XIAO ESP32S3 leverages dual-core ESP32S3 chip, supporting both Wi-Fi and BLE wireless connectivities, which allows battery charge. It integrates built-in camera sensor, digital microphone. It offers 8MB PSRAM, 8MB FLASH, and external SD card slot. All of these make it suitable for embedded ML, like intelligent voice and vision AI.
